// Logisim project cpu.circ as structural Verilog: 11 circuits, main circuit InstructionRAM
module main (
);

  wire alu_1_negative, alu_1_o1, alu_1_o2, alu_1_o3, alu_1_o4, alu_1_overflow, alu_1_zero, clock_1_out,
       dataram_1_o1, dataram_1_o2, dataram_1_o3, dataram_1_o4, incrementer_1_o1, incrementer_1_o2,
       incrementer_1_o3, instructionram_1_o1, instructionram_1_o2, instructionram_1_o3, instructionram_1_o4,
       ir_1_o1, ir_1_o2, ir_1_o3, ir_1_o4, pc_1_o1, pc_1_o2, pc_1_o3, undriven, undriven_2, undriven_3,
       undriven_4;

  Clock clock_1 (.out(clock_1_out));
  PC pc_1 (
    .Clock(clock_1_out), .Sequencer(1'b1), .D1(incrementer_1_o1), .D2(incrementer_1_o2),
    .D3(incrementer_1_o3), .O1(pc_1_o1), .O2(pc_1_o2), .O3(pc_1_o3));
  Incrementer incrementer_1 (
    .D1(pc_1_o1), .D2(pc_1_o2), .D3(pc_1_o3), .O1(incrementer_1_o1), .O2(incrementer_1_o2),
    .O3(incrementer_1_o3));
  InstructionRAM instructionram_1 (
    .Clock(clock_1_out), .Sequencer(1'b1), .A1(pc_1_o1), .A2(pc_1_o2), .A3(pc_1_o3),
    .O1(instructionram_1_o1), .O2(instructionram_1_o2), .O3(instructionram_1_o3), .O4(instructionram_1_o4));
  IR ir_1 (
    .Clock(clock_1_out), .Sequencer(1'b1), .D1(instructionram_1_o1), .D2(instructionram_1_o2),
    .D3(instructionram_1_o3), .D4(instructionram_1_o4), .O1(ir_1_o1), .O2(ir_1_o2), .O3(ir_1_o3), .O4(ir_1_o4));
  RegisterBlock registerblock_1 (
    .Clock(clock_1_out), .Sequencer(undriven), .A1(ir_1_o3), .A2(ir_1_o4), .D1(dataram_1_o1),
    .D2(dataram_1_o2), .D3(dataram_1_o3), .D4(dataram_1_o4));  // open: L1, L2, L3, L4, R1, R2, R3, R4
  StatusRegister statusregister_1 (
    .Clock(undriven_3), .Zero(alu_1_zero), .Negative(alu_1_negative), .Overflow(alu_1_overflow));  // open: Sequencer, out_6, out_7, out_8
  ALU alu_1 (
    .Clock(undriven_2), .Zero(alu_1_zero), .Negative(alu_1_negative), .Overflow(alu_1_overflow),
    .O1(alu_1_o1), .O2(alu_1_o2), .O3(alu_1_o3), .O4(alu_1_o4));  // open: Command, L1, L2, L3, L4, R1, R2, R3, R4
  DataRAM dataram_1 (
    .Sequencer(undriven_4), .D1(alu_1_o1), .D2(alu_1_o2), .D3(alu_1_o3), .D4(alu_1_o4), .O1(dataram_1_o1),
    .O2(dataram_1_o2), .O3(dataram_1_o3), .O4(dataram_1_o4));  // open: Clock, Address
endmodule

module InstructionRAM (
  input  Clock,
  input  Sequencer,
  input  A1,
  input  A2,
  input  A3,
  output O1,
  output O2,
  output O3,
  output O4
);

  wire and_1_out, and_2_out, and_3_out, and_4_out, and_5_out, and_6_out, and_7_out, and_8_out, and_9_out,
       and_10_out, and_11_out, and_12_out, and_13_out, and_14_out, and_15_out, and_16_out, and_17_out,
       and_18_out, and_19_out, and_20_out, and_21_out, and_22_out, and_23_out, and_24_out, and_25_out,
       and_26_out, and_27_out, and_28_out, and_29_out, and_30_out, and_31_out, and_32_out, and_33_out,
       and_34_out, and_35_out, and_36_out, and_37_out, and_38_out, and_39_out, and_40_out, and_41_out,
       and_42_out, and_43_out, and_44_out, and_45_out, and_46_out, and_47_out, and_48_out, and_49_out,
       and_50_out, and_51_out, and_52_out, and_53_out, and_54_out, and_55_out, and_56_out, and_57_out,
       and_58_out, and_59_out, and_60_out, and_61_out, and_62_out, and_63_out, and_64_out, and_65_out,
       and_66_out, and_67_out, and_68_out, and_69_out, and_70_out, and_71_out, and_72_out, and_73_out,
       and_74_out, and_75_out, and_76_out, and_77_out, and_78_out, and_79_out, and_80_out, d_ff_1_q,
       d_ff_2_q, d_ff_3_q, d_ff_4_q, d_ff_5_q, d_ff_6_q, d_ff_7_q, d_ff_8_q, d_ff_9_q, d_ff_10_q, d_ff_11_q,
       d_ff_12_q, d_ff_13_q, d_ff_14_q, d_ff_15_q, d_ff_16_q, d_ff_17_q, d_ff_18_q, d_ff_19_q, d_ff_20_q,
       d_ff_21_q, d_ff_22_q, d_ff_23_q, d_ff_24_q, d_ff_25_q, d_ff_26_q, d_ff_27_q, d_ff_28_q, d_ff_29_q,
       d_ff_30_q, d_ff_31_q, d_ff_32_q, d_ff_33_q, d_ff_34_q, d_ff_35_q, d_ff_36_q, d_ff_37_q, not_1_out,
       not_2_out, not_3_out, not_4_out, not_5_out, not_6_out, not_7_out, not_8_out, not_9_out, not_10_out,
       not_11_out, not_12_out, undriven, undriven_2, undriven_3, undriven_4;

  not not_1 (not_1_out, A3);
  not not_2 (not_2_out, A2);
  not not_3 (not_3_out, A2);
  not not_4 (not_4_out, A3);
  not not_5 (not_5_out, A1);
  not not_6 (not_6_out, A1);
  not not_7 (not_7_out, A3);
  not not_8 (not_8_out, A1);
  not not_9 (not_9_out, A2);
  not not_10 (not_10_out, A1);
  not not_11 (not_11_out, A2);
  not not_12 (not_12_out, A3);
  and and_1 (and_1_out, A1, A2, Clock, A3);
  and and_2 (and_2_out, and_1_out, 1'b0);
  and and_3 (and_3_out, A1, A2, Clock, not_1_out);
  and and_4 (and_4_out, and_3_out, 1'b0);
  and and_5 (and_5_out, A1, not_2_out, Clock, A3);
  and and_6 (and_6_out, and_5_out, 1'b0);
  and and_7 (and_7_out, A1, not_3_out, Clock, not_4_out);
  and and_8 (and_8_out, and_7_out, 1'b0);
  and and_9 (and_9_out, not_5_out, A2, Clock, A3);
  and and_10 (and_10_out, and_9_out, 1'b0);
  and and_11 (and_11_out, not_6_out, A2, Clock, not_7_out);
  and and_12 (and_12_out, and_11_out, 1'b0);
  and and_13 (and_13_out, not_8_out, not_9_out, Clock, A3);
  and and_14 (and_14_out, and_13_out, 1'b0);
  and and_15 (and_15_out, not_10_out, not_11_out, Clock, not_12_out);
  and and_16 (and_16_out, and_15_out, 1'b0);
  D_Flip_Flop #(.trigger("falling")) d_ff_1 (.D(Sequencer), .clk(Clock), .Q(d_ff_1_q));  // open: Qn, preset, reset
  and and_17 (and_17_out, and_1_out, 1'b0, d_ff_10_q);
  D_Flip_Flop #(.trigger("high")) d_ff_2 (.D(and_17_out), .clk(and_2_out), .Q(d_ff_2_q));  // open: Qn, preset, reset
  and and_18 (and_18_out, and_3_out, 1'b0, d_ff_10_q);
  D_Flip_Flop #(.trigger("high")) d_ff_3 (.D(and_18_out), .clk(and_4_out), .Q(d_ff_3_q));  // open: Qn, preset, reset
  and and_19 (and_19_out, and_5_out, 1'b0, d_ff_10_q);
  D_Flip_Flop #(.trigger("high")) d_ff_4 (.D(and_19_out), .clk(and_6_out), .Q(d_ff_4_q));  // open: Qn, preset, reset
  and and_20 (and_20_out, and_7_out, 1'b0, d_ff_10_q);
  D_Flip_Flop #(.trigger("high")) d_ff_5 (.D(and_20_out), .clk(and_8_out), .Q(d_ff_5_q));  // open: Qn, preset, reset
  and and_21 (and_21_out, and_9_out, 1'b0, d_ff_10_q);
  D_Flip_Flop #(.trigger("high")) d_ff_6 (.D(and_21_out), .clk(and_10_out), .Q(d_ff_6_q));  // open: Qn, preset, reset
  and and_22 (and_22_out, and_11_out, 1'b0, d_ff_10_q);
  D_Flip_Flop #(.trigger("high")) d_ff_7 (.D(and_22_out), .clk(and_12_out), .Q(d_ff_7_q));  // open: Qn, preset, reset
  and and_23 (and_23_out, and_13_out, 1'b0, d_ff_10_q);
  D_Flip_Flop #(.trigger("high")) d_ff_8 (.D(and_23_out), .clk(and_14_out), .Q(d_ff_8_q));  // open: Qn, preset, reset
  and and_24 (and_24_out, and_15_out, 1'b0, d_ff_10_q);
  D_Flip_Flop #(.trigger("high")) d_ff_9 (.D(and_24_out), .clk(and_16_out), .Q(d_ff_9_q));  // open: Qn, preset, reset
  or or_1 (O1, and_25_out, and_26_out, and_27_out, and_28_out, and_29_out, and_30_out, and_31_out, and_32_out);
  and and_25 (and_25_out, d_ff_2_q, and_1_out, d_ff_1_q);
  and and_26 (and_26_out, d_ff_3_q, and_3_out, d_ff_1_q);
  and and_27 (and_27_out, d_ff_4_q, and_5_out, d_ff_1_q);
  and and_28 (and_28_out, d_ff_5_q, and_7_out, d_ff_1_q);
  and and_29 (and_29_out, d_ff_6_q, and_9_out, d_ff_1_q);
  and and_30 (and_30_out, d_ff_7_q, and_11_out, d_ff_1_q);
  and and_31 (and_31_out, d_ff_8_q, and_13_out, d_ff_1_q);
  and and_32 (and_32_out, d_ff_9_q, and_15_out, d_ff_1_q);
  D_Flip_Flop #(.trigger("falling")) d_ff_10 (.D(undriven), .clk(Clock), .Q(d_ff_10_q));  // open: Qn, preset, reset
  D_Flip_Flop #(.trigger("falling")) d_ff_11 (.D(undriven_2), .clk(Clock), .Q(d_ff_11_q));  // open: Qn, preset, reset
  and and_33 (and_33_out, and_1_out, 1'b0, d_ff_11_q);
  D_Flip_Flop #(.trigger("high")) d_ff_12 (.D(and_33_out), .clk(and_2_out), .Q(d_ff_12_q));  // open: Qn, preset, reset
  and and_34 (and_34_out, and_3_out, 1'b0, d_ff_11_q);
  D_Flip_Flop #(.trigger("high")) d_ff_13 (.D(and_34_out), .clk(and_4_out), .Q(d_ff_13_q));  // open: Qn, preset, reset
  and and_35 (and_35_out, and_5_out, 1'b0, d_ff_11_q);
  D_Flip_Flop #(.trigger("high")) d_ff_14 (.D(and_35_out), .clk(and_6_out), .Q(d_ff_14_q));  // open: Qn, preset, reset
  and and_36 (and_36_out, and_7_out, 1'b0, d_ff_11_q);
  D_Flip_Flop #(.trigger("high")) d_ff_15 (.D(and_36_out), .clk(and_8_out), .Q(d_ff_15_q));  // open: Qn, preset, reset
  and and_37 (and_37_out, and_9_out, 1'b0, d_ff_11_q);
  D_Flip_Flop #(.trigger("high")) d_ff_16 (.D(and_37_out), .clk(and_10_out), .Q(d_ff_16_q));  // open: Qn, preset, reset
  and and_38 (and_38_out, and_11_out, 1'b0, d_ff_11_q);
  D_Flip_Flop #(.trigger("high")) d_ff_17 (.D(and_38_out), .clk(and_12_out), .Q(d_ff_17_q));  // open: Qn, preset, reset
  and and_39 (and_39_out, and_13_out, 1'b0, d_ff_11_q);
  D_Flip_Flop #(.trigger("high")) d_ff_18 (.D(and_39_out), .clk(and_14_out), .Q(d_ff_18_q));  // open: Qn, preset, reset
  and and_40 (and_40_out, and_15_out, 1'b0, d_ff_11_q);
  D_Flip_Flop #(.trigger("high")) d_ff_19 (.D(and_40_out), .clk(and_16_out), .Q(d_ff_19_q));  // open: Qn, preset, reset
  D_Flip_Flop #(.trigger("falling")) d_ff_20 (.D(undriven_3), .clk(Clock), .Q(d_ff_20_q));  // open: Qn, preset, reset
  or or_2 (O2, and_41_out, and_42_out, and_43_out, and_44_out, and_45_out, and_46_out, and_47_out, and_48_out);
  and and_41 (and_41_out, d_ff_12_q, and_1_out, d_ff_1_q);
  and and_42 (and_42_out, d_ff_13_q, and_3_out, d_ff_1_q);
  and and_43 (and_43_out, d_ff_14_q, and_5_out, d_ff_1_q);
  and and_44 (and_44_out, d_ff_15_q, and_7_out, d_ff_1_q);
  and and_45 (and_45_out, d_ff_16_q, and_9_out, d_ff_1_q);
  and and_46 (and_46_out, d_ff_17_q, and_11_out, d_ff_1_q);
  and and_47 (and_47_out, d_ff_18_q, and_13_out, d_ff_1_q);
  and and_48 (and_48_out, d_ff_19_q, and_15_out, d_ff_1_q);
  D_Flip_Flop #(.trigger("falling")) d_ff_21 (.D(undriven_4), .clk(Clock), .Q(d_ff_21_q));  // open: Qn, preset, reset
  and and_49 (and_49_out, and_1_out, 1'b0, d_ff_20_q);
  D_Flip_Flop #(.trigger("high")) d_ff_22 (.D(and_49_out), .clk(and_2_out), .Q(d_ff_22_q));  // open: Qn, preset, reset
  and and_50 (and_50_out, and_3_out, 1'b0, d_ff_20_q);
  D_Flip_Flop #(.trigger("high")) d_ff_23 (.D(and_50_out), .clk(and_4_out), .Q(d_ff_23_q));  // open: Qn, preset, reset
  and and_51 (and_51_out, and_5_out, 1'b0, d_ff_20_q);
  D_Flip_Flop #(.trigger("high")) d_ff_24 (.D(and_51_out), .clk(and_6_out), .Q(d_ff_24_q));  // open: Qn, preset, reset
  and and_52 (and_52_out, and_7_out, 1'b0, d_ff_20_q);
  D_Flip_Flop #(.trigger("high")) d_ff_25 (.D(and_52_out), .clk(and_8_out), .Q(d_ff_25_q));  // open: Qn, preset, reset
  and and_53 (and_53_out, and_9_out, 1'b0, d_ff_20_q);
  D_Flip_Flop #(.trigger("high")) d_ff_26 (.D(and_53_out), .clk(and_10_out), .Q(d_ff_26_q));  // open: Qn, preset, reset
  and and_54 (and_54_out, and_11_out, 1'b0, d_ff_20_q);
  D_Flip_Flop #(.trigger("high")) d_ff_27 (.D(and_54_out), .clk(and_12_out), .Q(d_ff_27_q));  // open: Qn, preset, reset
  and and_55 (and_55_out, and_13_out, 1'b0, d_ff_20_q);
  D_Flip_Flop #(.trigger("high")) d_ff_28 (.D(and_55_out), .clk(and_14_out), .Q(d_ff_28_q));  // open: Qn, preset, reset
  and and_56 (and_56_out, and_15_out, 1'b0, d_ff_20_q);
  D_Flip_Flop #(.trigger("high")) d_ff_29 (.D(and_56_out), .clk(and_16_out), .Q(d_ff_29_q));  // open: Qn, preset, reset
  or or_3 (O3, and_57_out, and_58_out, and_59_out, and_60_out, and_61_out, and_62_out, and_63_out, and_64_out);
  and and_57 (and_57_out, d_ff_22_q, and_1_out, d_ff_1_q);
  and and_58 (and_58_out, d_ff_23_q, and_3_out, d_ff_1_q);
  and and_59 (and_59_out, d_ff_24_q, and_5_out, d_ff_1_q);
  and and_60 (and_60_out, d_ff_25_q, and_7_out, d_ff_1_q);
  and and_61 (and_61_out, d_ff_26_q, and_9_out, d_ff_1_q);
  and and_62 (and_62_out, d_ff_27_q, and_11_out, d_ff_1_q);
  and and_63 (and_63_out, d_ff_28_q, and_13_out, d_ff_1_q);
  and and_64 (and_64_out, d_ff_29_q, and_15_out, d_ff_1_q);
  and and_65 (and_65_out, and_1_out, 1'b0, d_ff_21_q);
  D_Flip_Flop #(.trigger("high")) d_ff_30 (.D(and_65_out), .clk(and_2_out), .Q(d_ff_30_q));  // open: Qn, preset, reset
  and and_66 (and_66_out, and_3_out, 1'b0, d_ff_21_q);
  D_Flip_Flop #(.trigger("high")) d_ff_31 (.D(and_66_out), .clk(and_4_out), .Q(d_ff_31_q));  // open: Qn, preset, reset
  and and_67 (and_67_out, and_5_out, 1'b0, d_ff_21_q);
  D_Flip_Flop #(.trigger("high")) d_ff_32 (.D(and_67_out), .clk(and_6_out), .Q(d_ff_32_q));  // open: Qn, preset, reset
  and and_68 (and_68_out, and_7_out, 1'b0, d_ff_21_q);
  D_Flip_Flop #(.trigger("high")) d_ff_33 (.D(and_68_out), .clk(and_8_out), .Q(d_ff_33_q));  // open: Qn, preset, reset
  and and_69 (and_69_out, and_9_out, 1'b0, d_ff_21_q);
  D_Flip_Flop #(.trigger("high")) d_ff_34 (.D(and_69_out), .clk(and_10_out), .Q(d_ff_34_q));  // open: Qn, preset, reset
  and and_70 (and_70_out, and_11_out, 1'b0, d_ff_21_q);
  D_Flip_Flop #(.trigger("high")) d_ff_35 (.D(and_70_out), .clk(and_12_out), .Q(d_ff_35_q));  // open: Qn, preset, reset
  and and_71 (and_71_out, and_13_out, 1'b0, d_ff_21_q);
  D_Flip_Flop #(.trigger("high")) d_ff_36 (.D(and_71_out), .clk(and_14_out), .Q(d_ff_36_q));  // open: Qn, preset, reset
  and and_72 (and_72_out, and_15_out, 1'b0, d_ff_21_q);
  D_Flip_Flop #(.trigger("high")) d_ff_37 (.D(and_72_out), .clk(and_16_out), .Q(d_ff_37_q));  // open: Qn, preset, reset
  or or_4 (O4, and_73_out, and_74_out, and_75_out, and_76_out, and_77_out, and_78_out, and_79_out, and_80_out);
  and and_73 (and_73_out, d_ff_30_q, and_1_out, d_ff_1_q);
  and and_74 (and_74_out, d_ff_31_q, and_3_out, d_ff_1_q);
  and and_75 (and_75_out, d_ff_32_q, and_5_out, d_ff_1_q);
  and and_76 (and_76_out, d_ff_33_q, and_7_out, d_ff_1_q);
  and and_77 (and_77_out, d_ff_34_q, and_9_out, d_ff_1_q);
  and and_78 (and_78_out, d_ff_35_q, and_11_out, d_ff_1_q);
  and and_79 (and_79_out, d_ff_36_q, and_13_out, d_ff_1_q);
  and and_80 (and_80_out, d_ff_37_q, and_15_out, d_ff_1_q);

  // Notes on the sheet:
  //   3-bit address input pins
  //   Mode input pin
  //   4-bit data input pins
  //   4-bit data output pins
endmodule

module ALU (
  input  Clock,
  input  Command,
  input  L1,
  input  L2,
  input  L3,
  input  L4,
  input  R1,
  input  R2,
  input  R3,
  input  R4,
  output Zero,
  output Negative,
  output Overflow,
  output O1,
  output O2,
  output O3,
  output O4
);

  wire and_1_out, and_2_out, and_3_out, and_4_out, and_5_out, and_6_out, and_7_out, and_8_out, and_9_out,
       and_10_out, and_11_out, and_12_out, and_13_out, and_14_out, and_15_out, and_16_out, and_17_out,
       and_18_out, and_19_out, and_20_out, and_21_out, and_22_out, and_23_out, and_24_out, and_25_out,
       and_27_out, fulladder_1_c, fulladder_2_c, fulladder_3_c, Neg_out, not_1_out, not_2_out, not_3_out,
       not_4_out, not_5_out, not_6_out, not_7_out, not_8_out, not_9_out, not_10_out, not_11_out, not_12_out,
       not_13_out, not_14_out, not_15_out, or_1_out, or_2_out, or_3_out, or_4_out, or_5_out, Pos_out,
       xor_2_out, xor_3_out, xor_4_out, xor_5_out;

  not not_1 (not_1_out, Command);
  and and_1 (and_1_out, L1, Clock);
  FullAdder fulladder_1 (.A(or_1_out), .B(and_1_out), .Carry(fulladder_2_c), .C(fulladder_1_c), .Sum(Negative));
  and and_2 (and_2_out, L2, Clock);
  and and_3 (and_3_out, L3, Clock);
  and and_4 (and_4_out, L4, Clock);
  FullAdder fulladder_2 (.A(or_2_out), .B(and_2_out), .Carry(fulladder_3_c), .C(fulladder_2_c), .Sum(O2));
  or or_1 (or_1_out, xor_2_out, and_6_out);
  or or_2 (or_2_out, xor_3_out, and_7_out);
  and and_5 (and_5_out, and_4_out, or_4_out);
  FullAdder fulladder_3 (.A(or_3_out), .B(and_3_out), .Carry(and_5_out), .C(fulladder_3_c), .Sum(O3));
  or or_3 (or_3_out, xor_4_out, and_9_out);
  or or_4 (or_4_out, xor_5_out, and_10_out);
  xor xor_1 (O4, and_4_out, or_4_out);
  and and_6 (and_6_out, and_13_out, not_1_out);
  and and_7 (and_7_out, and_14_out, not_1_out);
  and and_8 (and_8_out, not_6_out, and_11_out);
  xor xor_2 (xor_2_out, not_6_out, and_11_out);
  not not_2 (not_2_out, O4);
  not not_3 (not_3_out, O3);
  not not_4 (not_4_out, O2);
  not not_5 (not_5_out, Negative);
  and and_9 (and_9_out, and_15_out, not_1_out);
  and and_10 (and_10_out, and_20_out, not_1_out);
  and and_11 (and_11_out, not_7_out, and_19_out);
  xor xor_3 (xor_3_out, not_7_out, and_19_out);
  and and_12 (and_12_out, not_2_out, not_3_out, not_4_out, not_5_out);
  and and_13 (and_13_out, R1, Clock);
  and and_14 (and_14_out, R2, Clock);
  and and_15 (and_15_out, R3, Clock);
  and and_16 (and_16_out, and_13_out, Command);
  and and_17 (and_17_out, and_14_out, Command);
  and and_18 (and_18_out, and_15_out, Command);
  not not_6 (not_6_out, and_16_out);
  not not_7 (not_7_out, and_17_out);
  not not_8 (not_8_out, and_18_out);
  and and_19 (and_19_out, not_8_out, and_22_out);
  xor xor_4 (xor_4_out, not_8_out, and_22_out);
  and Neg (Neg_out, or_1_out, and_1_out);
  not not_9 (not_9_out, or_1_out);
  and Pos (Pos_out, not_9_out, not_10_out);
  not not_10 (not_10_out, and_1_out);
  not not_11 (not_11_out, or_1_out);
  and and_20 (and_20_out, R4, Clock);
  and and_21 (and_21_out, and_20_out, Command);
  not not_12 (not_12_out, and_21_out);
  xor xor_5 (xor_5_out, not_12_out, 1'b1);
  and and_22 (and_22_out, not_12_out, 1'b1);
  and and_23 (and_23_out, Negative, Neg_out);
  and and_24 (and_24_out, Pos_out, Negative);
  and and_25 (and_25_out, not_13_out, not_11_out, fulladder_1_c);
  not not_13 (not_13_out, Command);
  and and_26 (Zero, and_12_out, Clock);
  or or_5 (or_5_out, and_25_out, and_24_out, and_27_out);
  not not_14 (not_14_out, fulladder_1_c);
  and and_27 (and_27_out, and_23_out, not_14_out);
  not not_15 (not_15_out, Zero);
  and notZero (Overflow, or_5_out, not_15_out);

  assign O1 = Negative;

  // Other names for the same wires on the sheet: CMD = Command

  // Notes on the sheet:
  //   Add/Sub command
  //   0 add, 1 sub
  //   B Input
  //   L input
  //   A-out output
  //   Adder
  //   A Input
  //   R Input
  //   2's Complement
  //   Status output
  //   -8 + -8 is underflow (not supported)
endmodule

module FullAdder (
  input  A,
  input  B,
  input  Carry,
  output C,
  output Sum
);

  wire and_1_out, and_2_out, xor_1_out;

  and and_1 (and_1_out, A, B);
  xor xor_1 (xor_1_out, A, B);
  and and_2 (and_2_out, xor_1_out, Carry);
  or or_1 (C, and_1_out, and_2_out);
  xor xor_2 (Sum, xor_1_out, Carry);
endmodule

module PC (
  input  Clock,
  input  Sequencer,
  input  D1,
  input  D2,
  input  D3,
  output O1,
  output O2,
  output O3
);

  wire and_1_out;

  and and_1 (and_1_out, Clock, Sequencer);
  D_Flip_Flop d_ff_1 (.D(D1), .clk(and_1_out), .Q(O1));  // open: Qn, preset, reset
  D_Flip_Flop d_ff_2 (.D(D2), .clk(and_1_out), .Q(O2));  // open: Qn, preset, reset
  D_Flip_Flop d_ff_3 (.D(D3), .clk(and_1_out), .Q(O3));  // open: Qn, preset, reset
endmodule

module DataRAM (
  input  Sequencer,
  input  Clock,
  input  Address,
  input  D1,
  input  D2,
  input  D3,
  input  D4,
  output O1,
  output O2,
  output O3,
  output O4
);

  wire and_1_out, and_2_out, and_3_out, and_4_out, and_5_out, and_6_out, and_7_out, and_8_out, and_9_out,
       and_10_out, and_11_out, and_12_out, and_13_out, and_14_out, and_15_out, and_16_out, and_17_out,
       and_18_out, and_19_out, and_20_out, and_21_out, and_22_out, and_23_out, and_24_out, and_25_out,
       and_26_out, and_27_out, and_28_out, and_29_out, and_30_out, and_31_out, and_32_out, and_33_out,
       and_34_out, and_35_out, and_36_out, and_37_out, and_38_out, and_39_out, and_40_out, and_41_out,
       and_42_out, and_43_out, and_44_out, and_45_out, and_46_out, and_47_out, and_48_out, and_49_out,
       and_50_out, and_51_out, and_52_out, and_53_out, and_54_out, and_55_out, and_56_out, and_57_out,
       and_58_out, and_59_out, and_60_out, and_61_out, and_62_out, and_63_out, and_64_out, and_65_out,
       and_66_out, and_67_out, and_68_out, and_69_out, and_70_out, and_71_out, and_72_out, and_73_out,
       and_74_out, and_75_out, and_76_out, and_77_out, and_78_out, and_79_out, and_80_out, d_ff_1_q,
       d_ff_2_q, d_ff_3_q, d_ff_4_q, d_ff_5_q, d_ff_6_q, d_ff_7_q, d_ff_8_q, d_ff_9_q, d_ff_10_q, d_ff_11_q,
       d_ff_12_q, d_ff_13_q, d_ff_14_q, d_ff_15_q, d_ff_16_q, d_ff_17_q, d_ff_18_q, d_ff_19_q, d_ff_20_q,
       d_ff_25_q, d_ff_26_q, d_ff_27_q, d_ff_28_q, d_ff_29_q, d_ff_30_q, d_ff_31_q, d_ff_32_q, d_ff_33_q,
       d_ff_34_q, d_ff_35_q, d_ff_36_q, d_ff_37_q, d_ff_38_q, d_ff_39_q, d_ff_40_q, not_1_out, not_2_out,
       not_3_out, not_4_out, not_5_out, not_6_out, not_7_out, not_8_out, not_9_out, not_10_out, not_11_out,
       not_12_out, or_1_out, or_2_out, or_3_out, or_4_out, undriven, undriven_2;

  D_Flip_Flop #(.trigger("falling")) d_ff_1 (.D(undriven), .clk(Clock), .Q(d_ff_1_q));  // open: Qn, preset, reset
  D_Flip_Flop #(.trigger("falling")) d_ff_2 (.D(undriven_2), .clk(Clock), .Q(d_ff_2_q));  // open: Qn, preset, reset
  not not_1 (not_1_out, d_ff_3_q);
  not not_2 (not_2_out, d_ff_2_q);
  not not_3 (not_3_out, d_ff_2_q);
  not not_4 (not_4_out, d_ff_3_q);
  not not_5 (not_5_out, d_ff_1_q);
  not not_6 (not_6_out, d_ff_1_q);
  not not_7 (not_7_out, d_ff_3_q);
  not not_8 (not_8_out, d_ff_1_q);
  not not_9 (not_9_out, d_ff_2_q);
  not not_10 (not_10_out, d_ff_1_q);
  not not_11 (not_11_out, d_ff_2_q);
  not not_12 (not_12_out, d_ff_3_q);
  D_Flip_Flop #(.trigger("falling")) d_ff_3 (.D(Address), .clk(Clock), .Q(d_ff_3_q));  // open: Qn, preset, reset
  and and_1 (and_1_out, d_ff_1_q, d_ff_2_q, Clock, d_ff_3_q);
  and and_2 (and_2_out, and_1_out, d_ff_4_q);
  and and_3 (and_3_out, d_ff_1_q, d_ff_2_q, Clock, not_1_out);
  and and_4 (and_4_out, and_3_out, d_ff_4_q);
  and and_5 (and_5_out, d_ff_1_q, not_2_out, Clock, d_ff_3_q);
  and and_6 (and_6_out, and_5_out, d_ff_4_q);
  and and_7 (and_7_out, d_ff_1_q, not_3_out, Clock, not_4_out);
  and and_8 (and_8_out, and_7_out, d_ff_4_q);
  and and_9 (and_9_out, not_5_out, d_ff_2_q, Clock, d_ff_3_q);
  and and_10 (and_10_out, and_9_out, d_ff_4_q);
  and and_11 (and_11_out, not_6_out, d_ff_2_q, Clock, not_7_out);
  and and_12 (and_12_out, and_11_out, d_ff_4_q);
  and and_13 (and_13_out, not_8_out, not_9_out, Clock, d_ff_3_q);
  and and_14 (and_14_out, and_13_out, d_ff_4_q);
  and and_15 (and_15_out, not_10_out, not_11_out, Clock, not_12_out);
  and and_16 (and_16_out, and_15_out, d_ff_4_q);
  D_Flip_Flop #(.trigger("falling")) d_ff_4 (.D(Sequencer), .clk(Clock), .Q(d_ff_4_q));  // open: Qn, preset, reset
  and and_17 (and_17_out, and_1_out, d_ff_4_q, D1);
  D_Flip_Flop #(.trigger("high")) d_ff_5 (.D(and_17_out), .clk(and_2_out), .Q(d_ff_5_q));  // open: Qn, preset, reset
  and and_18 (and_18_out, and_3_out, d_ff_4_q, D1);
  D_Flip_Flop #(.trigger("high")) d_ff_6 (.D(and_18_out), .clk(and_4_out), .Q(d_ff_6_q));  // open: Qn, preset, reset
  and and_19 (and_19_out, and_5_out, d_ff_4_q, D1);
  D_Flip_Flop #(.trigger("high")) d_ff_7 (.D(and_19_out), .clk(and_6_out), .Q(d_ff_7_q));  // open: Qn, preset, reset
  and and_20 (and_20_out, and_7_out, d_ff_4_q, D1);
  D_Flip_Flop #(.trigger("high")) d_ff_8 (.D(and_20_out), .clk(and_8_out), .Q(d_ff_8_q));  // open: Qn, preset, reset
  and and_21 (and_21_out, and_9_out, d_ff_4_q, D1);
  D_Flip_Flop #(.trigger("high")) d_ff_9 (.D(and_21_out), .clk(and_10_out), .Q(d_ff_9_q));  // open: Qn, preset, reset
  and and_22 (and_22_out, and_11_out, d_ff_4_q, D1);
  D_Flip_Flop #(.trigger("high")) d_ff_10 (.D(and_22_out), .clk(and_12_out), .Q(d_ff_10_q));  // open: Qn, preset, reset
  and and_23 (and_23_out, and_13_out, d_ff_4_q, D1);
  D_Flip_Flop #(.trigger("high")) d_ff_11 (.D(and_23_out), .clk(and_14_out), .Q(d_ff_11_q));  // open: Qn, preset, reset
  and and_24 (and_24_out, and_15_out, d_ff_4_q, D1);
  D_Flip_Flop #(.trigger("high")) d_ff_12 (.D(and_24_out), .clk(and_16_out), .Q(d_ff_12_q));  // open: Qn, preset, reset
  or or_1 (or_1_out, and_25_out, and_26_out, and_27_out, and_28_out, and_29_out, and_30_out, and_31_out, and_32_out);
  and and_25 (and_25_out, d_ff_5_q, and_1_out, 1'b1);
  and and_26 (and_26_out, d_ff_6_q, and_3_out, 1'b1);
  and and_27 (and_27_out, d_ff_7_q, and_5_out, 1'b1);
  and and_28 (and_28_out, d_ff_8_q, and_7_out, 1'b1);
  and and_29 (and_29_out, d_ff_9_q, and_9_out, 1'b1);
  and and_30 (and_30_out, d_ff_10_q, and_11_out, 1'b1);
  and and_31 (and_31_out, d_ff_11_q, and_13_out, 1'b1);
  and and_32 (and_32_out, d_ff_12_q, and_15_out, 1'b1);
  and and_33 (and_33_out, and_1_out, d_ff_4_q, D2);
  D_Flip_Flop #(.trigger("high")) d_ff_13 (.D(and_33_out), .clk(and_2_out), .Q(d_ff_13_q));  // open: Qn, preset, reset
  and and_34 (and_34_out, and_3_out, d_ff_4_q, D2);
  D_Flip_Flop #(.trigger("high")) d_ff_14 (.D(and_34_out), .clk(and_4_out), .Q(d_ff_14_q));  // open: Qn, preset, reset
  and and_35 (and_35_out, and_5_out, d_ff_4_q, D2);
  D_Flip_Flop #(.trigger("high")) d_ff_15 (.D(and_35_out), .clk(and_6_out), .Q(d_ff_15_q));  // open: Qn, preset, reset
  and and_36 (and_36_out, and_7_out, d_ff_4_q, D2);
  D_Flip_Flop #(.trigger("high")) d_ff_16 (.D(and_36_out), .clk(and_8_out), .Q(d_ff_16_q));  // open: Qn, preset, reset
  and and_37 (and_37_out, and_9_out, d_ff_4_q, D2);
  D_Flip_Flop #(.trigger("high")) d_ff_17 (.D(and_37_out), .clk(and_10_out), .Q(d_ff_17_q));  // open: Qn, preset, reset
  and and_38 (and_38_out, and_11_out, d_ff_4_q, D2);
  D_Flip_Flop #(.trigger("high")) d_ff_18 (.D(and_38_out), .clk(and_12_out), .Q(d_ff_18_q));  // open: Qn, preset, reset
  and and_39 (and_39_out, and_13_out, d_ff_4_q, D2);
  D_Flip_Flop #(.trigger("high")) d_ff_19 (.D(and_39_out), .clk(and_14_out), .Q(d_ff_19_q));  // open: Qn, preset, reset
  and and_40 (and_40_out, and_15_out, d_ff_4_q, D2);
  D_Flip_Flop #(.trigger("high")) d_ff_20 (.D(and_40_out), .clk(and_16_out), .Q(d_ff_20_q));  // open: Qn, preset, reset
  D_Flip_Flop #(.trigger("high")) d_ff_21 (.D(or_1_out), .clk(Clock), .Q(O1));  // open: Qn, preset, reset
  or or_2 (or_2_out, and_41_out, and_42_out, and_43_out, and_44_out, and_45_out, and_46_out, and_47_out, and_48_out);
  and and_41 (and_41_out, d_ff_13_q, and_1_out, 1'b1);
  and and_42 (and_42_out, d_ff_14_q, and_3_out, 1'b1);
  and and_43 (and_43_out, d_ff_15_q, and_5_out, 1'b1);
  and and_44 (and_44_out, d_ff_16_q, and_7_out, 1'b1);
  and and_45 (and_45_out, d_ff_17_q, and_9_out, 1'b1);
  and and_46 (and_46_out, d_ff_18_q, and_11_out, 1'b1);
  and and_47 (and_47_out, d_ff_19_q, and_13_out, 1'b1);
  and and_48 (and_48_out, d_ff_20_q, and_15_out, 1'b1);
  D_Flip_Flop #(.trigger("high")) d_ff_22 (.D(or_2_out), .clk(Clock), .Q(O2));  // open: Qn, preset, reset
  D_Flip_Flop #(.trigger("high")) d_ff_23 (.D(or_3_out), .clk(Clock), .Q(O3));  // open: Qn, preset, reset
  D_Flip_Flop #(.trigger("high")) d_ff_24 (.D(or_4_out), .clk(Clock), .Q(O4));  // open: Qn, preset, reset
  and and_49 (and_49_out, and_1_out, d_ff_4_q, D3);
  D_Flip_Flop #(.trigger("high")) d_ff_25 (.D(and_49_out), .clk(and_2_out), .Q(d_ff_25_q));  // open: Qn, preset, reset
  and and_50 (and_50_out, and_3_out, d_ff_4_q, D3);
  D_Flip_Flop #(.trigger("high")) d_ff_26 (.D(and_50_out), .clk(and_4_out), .Q(d_ff_26_q));  // open: Qn, preset, reset
  and and_51 (and_51_out, and_5_out, d_ff_4_q, D3);
  D_Flip_Flop #(.trigger("high")) d_ff_27 (.D(and_51_out), .clk(and_6_out), .Q(d_ff_27_q));  // open: Qn, preset, reset
  and and_52 (and_52_out, and_7_out, d_ff_4_q, D3);
  D_Flip_Flop #(.trigger("high")) d_ff_28 (.D(and_52_out), .clk(and_8_out), .Q(d_ff_28_q));  // open: Qn, preset, reset
  and and_53 (and_53_out, and_9_out, d_ff_4_q, D3);
  D_Flip_Flop #(.trigger("high")) d_ff_29 (.D(and_53_out), .clk(and_10_out), .Q(d_ff_29_q));  // open: Qn, preset, reset
  and and_54 (and_54_out, and_11_out, d_ff_4_q, D3);
  D_Flip_Flop #(.trigger("high")) d_ff_30 (.D(and_54_out), .clk(and_12_out), .Q(d_ff_30_q));  // open: Qn, preset, reset
  and and_55 (and_55_out, and_13_out, d_ff_4_q, D3);
  D_Flip_Flop #(.trigger("high")) d_ff_31 (.D(and_55_out), .clk(and_14_out), .Q(d_ff_31_q));  // open: Qn, preset, reset
  and and_56 (and_56_out, and_15_out, d_ff_4_q, D3);
  D_Flip_Flop #(.trigger("high")) d_ff_32 (.D(and_56_out), .clk(and_16_out), .Q(d_ff_32_q));  // open: Qn, preset, reset
  or or_3 (or_3_out, and_57_out, and_58_out, and_59_out, and_60_out, and_61_out, and_62_out, and_63_out, and_64_out);
  and and_57 (and_57_out, d_ff_25_q, and_1_out, 1'b1);
  and and_58 (and_58_out, d_ff_26_q, and_3_out, 1'b1);
  and and_59 (and_59_out, d_ff_27_q, and_5_out, 1'b1);
  and and_60 (and_60_out, d_ff_28_q, and_7_out, 1'b1);
  and and_61 (and_61_out, d_ff_29_q, and_9_out, 1'b1);
  and and_62 (and_62_out, d_ff_30_q, and_11_out, 1'b1);
  and and_63 (and_63_out, d_ff_31_q, and_13_out, 1'b1);
  and and_64 (and_64_out, d_ff_32_q, and_15_out, 1'b1);
  and and_65 (and_65_out, and_1_out, d_ff_4_q, D4);
  D_Flip_Flop #(.trigger("high")) d_ff_33 (.D(and_65_out), .clk(and_2_out), .Q(d_ff_33_q));  // open: Qn, preset, reset
  and and_66 (and_66_out, and_3_out, d_ff_4_q, D4);
  D_Flip_Flop #(.trigger("high")) d_ff_34 (.D(and_66_out), .clk(and_4_out), .Q(d_ff_34_q));  // open: Qn, preset, reset
  and and_67 (and_67_out, and_5_out, d_ff_4_q, D4);
  D_Flip_Flop #(.trigger("high")) d_ff_35 (.D(and_67_out), .clk(and_6_out), .Q(d_ff_35_q));  // open: Qn, preset, reset
  and and_68 (and_68_out, and_7_out, d_ff_4_q, D4);
  D_Flip_Flop #(.trigger("high")) d_ff_36 (.D(and_68_out), .clk(and_8_out), .Q(d_ff_36_q));  // open: Qn, preset, reset
  and and_69 (and_69_out, and_9_out, d_ff_4_q, D4);
  D_Flip_Flop #(.trigger("high")) d_ff_37 (.D(and_69_out), .clk(and_10_out), .Q(d_ff_37_q));  // open: Qn, preset, reset
  and and_70 (and_70_out, and_11_out, d_ff_4_q, D4);
  D_Flip_Flop #(.trigger("high")) d_ff_38 (.D(and_70_out), .clk(and_12_out), .Q(d_ff_38_q));  // open: Qn, preset, reset
  and and_71 (and_71_out, and_13_out, d_ff_4_q, D4);
  D_Flip_Flop #(.trigger("high")) d_ff_39 (.D(and_71_out), .clk(and_14_out), .Q(d_ff_39_q));  // open: Qn, preset, reset
  and and_72 (and_72_out, and_15_out, d_ff_4_q, D4);
  D_Flip_Flop #(.trigger("high")) d_ff_40 (.D(and_72_out), .clk(and_16_out), .Q(d_ff_40_q));  // open: Qn, preset, reset
  or or_4 (or_4_out, and_73_out, and_74_out, and_75_out, and_76_out, and_77_out, and_78_out, and_79_out, and_80_out);
  and and_73 (and_73_out, d_ff_33_q, and_1_out, 1'b1);
  and and_74 (and_74_out, d_ff_34_q, and_3_out, 1'b1);
  and and_75 (and_75_out, d_ff_35_q, and_5_out, 1'b1);
  and and_76 (and_76_out, d_ff_36_q, and_7_out, 1'b1);
  and and_77 (and_77_out, d_ff_37_q, and_9_out, 1'b1);
  and and_78 (and_78_out, d_ff_38_q, and_11_out, 1'b1);
  and and_79 (and_79_out, d_ff_39_q, and_13_out, 1'b1);
  and and_80 (and_80_out, d_ff_40_q, and_15_out, 1'b1);

  // Notes on the sheet:
  //   3-bit address input pins
  //   Mode input pin
  //   4-bit data input pins
  //   4-bit data output pins
endmodule

module GeneralRegister (
  input  Clock,
  input  Sequencer,
  input  D1,
  input  D2,
  input  D3,
  input  D4,
  output O1,
  output O2,
  output O3,
  output O4
);

  wire and_1_out;

  and and_1 (and_1_out, Clock, Sequencer);
  D_Flip_Flop d_ff_1 (.D(D1), .clk(and_1_out), .Q(O1));  // open: Qn, preset, reset
  D_Flip_Flop d_ff_2 (.D(D2), .clk(and_1_out), .Q(O2));  // open: Qn, preset, reset
  D_Flip_Flop d_ff_3 (.D(D3), .clk(and_1_out), .Q(O3));  // open: Qn, preset, reset
  D_Flip_Flop d_ff_4 (.D(D4), .clk(and_1_out), .Q(O4));  // open: Qn, preset, reset
endmodule

module IR (
  input  Clock,
  input  Sequencer,
  input  D1,
  input  D2,
  input  D3,
  input  D4,
  output O1,
  output O2,
  output O3,
  output O4
);

  wire and_1_out;

  D_Flip_Flop d_ff_1 (.D(D1), .clk(and_1_out), .Q(O1));  // open: Qn, preset, reset
  D_Flip_Flop d_ff_2 (.D(D2), .clk(and_1_out), .Q(O2));  // open: Qn, preset, reset
  D_Flip_Flop d_ff_3 (.D(D3), .clk(and_1_out), .Q(O3));  // open: Qn, preset, reset
  D_Flip_Flop d_ff_4 (.D(D4), .clk(and_1_out), .Q(O4));  // open: Qn, preset, reset
  and and_1 (and_1_out, Clock, Sequencer);
endmodule

module Incrementer (
  input  D1,
  input  D2,
  input  D3,
  output O1,
  output O2,
  output O3
);

  wire fulladder_1_c, fulladder_2_c;

  FullAdder fulladder_1 (.A(1'b1), .B(D3), .C(fulladder_1_c), .Sum(O3));  // open: Carry
  FullAdder fulladder_2 (.A(fulladder_1_c), .B(D2), .C(fulladder_2_c), .Sum(O2));  // open: Carry
  FullAdder fulladder_3 (.A(fulladder_2_c), .B(D1), .Sum(O1));  // open: Carry, C
endmodule

module StatusRegister (
  input  Clock,
  input  Sequencer,
  input  Zero,
  input  Negative,
  input  Overflow,
  output out_6,
  output out_7,
  output out_8
);

  wire and_1_out;

  and and_1 (and_1_out, Clock, Sequencer);
  D_Flip_Flop d_ff_1 (.D(Zero), .clk(and_1_out), .Q(out_6));  // open: Qn, preset, reset
  D_Flip_Flop d_ff_2 (.D(Negative), .clk(and_1_out), .Q(out_7));  // open: Qn, preset, reset
  D_Flip_Flop d_ff_3 (.D(Overflow), .clk(and_1_out), .Q(out_8));  // open: Qn, preset, reset
endmodule

module RegisterBlock (
  input  Clock,
  input  Sequencer,
  input  A1,
  input  A2,
  input  D1,
  input  D2,
  input  D3,
  input  D4,
  output L1,
  output L2,
  output L3,
  output L4,
  output R1,
  output R2,
  output R3,
  output R4
);

  wire and_1_out, and_2_out, and_3_out, and_4_out, and_5_out, and_6_out, and_7_out, and_8_out, and_9_out,
       and_10_out, and_11_out, and_12_out, and_13_out, and_14_out, and_15_out, and_16_out, and_17_out,
       and_18_out, not_1_out, not_2_out, not_3_out, Register0_o1, Register0_o2, Register0_o3, Register0_o4,
       Register1_o1, Register1_o2, Register1_o3, Register1_o4;

  and and_1 (and_1_out, A1, Sequencer);
  not not_1 (not_1_out, A1);
  and and_2 (and_2_out, not_1_out, Sequencer);
  GeneralRegister Register0 (
    .Clock(Clock), .Sequencer(and_2_out), .D1(D1), .D2(D2), .D3(D3), .D4(D4), .O1(Register0_o1),
    .O2(Register0_o2), .O3(Register0_o3), .O4(Register0_o4));
  GeneralRegister Register1 (
    .Clock(Clock), .Sequencer(and_1_out), .D1(D1), .D2(D2), .D3(D3), .D4(D4), .O1(Register1_o1),
    .O2(Register1_o2), .O3(Register1_o3), .O4(Register1_o4));
  not not_2 (not_2_out, not_1_out);
  not not_3 (not_3_out, A2);
  and and_3 (and_3_out, not_1_out, Register0_o1);
  and and_4 (and_4_out, not_1_out, Register0_o2);
  and and_5 (and_5_out, not_1_out, Register0_o3);
  and and_6 (and_6_out, not_1_out, Register0_o4);
  and and_7 (and_7_out, not_2_out, Register1_o1);
  and and_8 (and_8_out, not_2_out, Register1_o2);
  and and_9 (and_9_out, not_2_out, Register1_o3);
  and and_10 (and_10_out, not_2_out, Register1_o4);
  and and_11 (and_11_out, A2, Register1_o1);
  and and_12 (and_12_out, A2, Register1_o2);
  and and_13 (and_13_out, A2, Register1_o3);
  and and_14 (and_14_out, A2, Register1_o4);
  and and_15 (and_15_out, not_3_out, Register0_o1);
  and and_16 (and_16_out, not_3_out, Register0_o2);
  and and_17 (and_17_out, not_3_out, Register0_o3);
  and and_18 (and_18_out, not_3_out, Register0_o4);
  or or_1 (L1, and_3_out, and_7_out);
  or or_2 (L2, and_4_out, and_8_out);
  or or_3 (L3, and_5_out, and_9_out);
  or or_4 (L4, and_6_out, and_10_out);
  or or_5 (R1, and_11_out, and_15_out);
  or or_6 (R2, and_12_out, and_16_out);
  or or_7 (R3, and_13_out, and_17_out);
  or or_8 (R4, and_14_out, and_18_out);
endmodule
