// Logisim project cu.circ as structural Verilog
module main (
);

  instruction_ram instruction_ram_1 ();  // open: CLK, DOUT1, DOUT2, DOUT3, DOUT4, MODE, ADDR1, ADDR2, ADDR3, DIN1, DIN2, DIN3, DIN4
endmodule

module instruction_ram (
  input  MODE,
  input  ADDR1,
  input  ADDR2,
  input  ADDR3,
  input  DIN1,
  input  DIN2,
  input  DIN3,
  input  DIN4,
  input  CLK,
  output DOUT1,
  output DOUT2,
  output DOUT3,
  output DOUT4
);

  wire and_1_out, and_2_out, and_3_out, and_4_out, and_5_out, and_6_out, and_7_out, and_8_out, and_9_out,
       and_10_out, and_11_out, and_12_out, and_13_out, and_14_out, and_15_out, and_16_out, and_17_out,
       and_18_out, and_19_out, and_20_out, and_21_out, and_22_out, and_23_out, and_24_out, and_25_out,
       and_26_out, and_27_out, and_28_out, and_29_out, and_30_out, and_31_out, and_32_out, and_33_out,
       and_34_out, and_35_out, and_36_out, and_37_out, and_38_out, and_39_out, and_40_out, and_41_out,
       and_42_out, and_43_out, and_44_out, and_45_out, and_46_out, and_47_out, and_48_out, and_49_out,
       and_50_out, and_51_out, and_52_out, and_53_out, and_54_out, and_55_out, and_56_out, and_57_out,
       and_58_out, and_59_out, and_60_out, and_61_out, and_62_out, and_63_out, and_64_out, and_65_out,
       and_66_out, and_67_out, and_68_out, and_69_out, and_70_out, and_71_out, and_72_out, and_73_out,
       and_74_out, and_75_out, and_76_out, and_77_out, and_78_out, and_79_out, and_80_out, and_81_out,
       and_82_out, and_83_out, and_84_out, and_85_out, and_86_out, and_87_out, and_88_out, and_89_out,
       and_90_out, and_91_out, and_92_out, and_93_out, and_94_out, and_95_out, and_96_out, and_97_out,
       and_98_out, and_99_out, and_100_out, and_101_out, and_102_out, and_103_out, and_104_out, and_105_out,
       d_ff_1_q, d_ff_2_q, d_ff_3_q, d_ff_4_q, d_ff_5_q, d_ff_6_q, d_ff_7_q, d_ff_8_q, not_1_out, not_2_out,
       not_3_out, not_4_out, not_5_out, not_6_out, not_7_out, not_8_out, not_9_out, not_10_out, not_11_out,
       not_12_out, not_13_out, not_14_out, not_15_out, not_16_out, not_17_out, not_18_out, not_19_out,
       not_20_out, not_21_out, not_22_out, not_23_out, not_24_out, not_25_out, not_26_out, not_27_out,
       not_28_out, not_29_out, not_30_out, not_31_out, not_32_out, not_33_out, not_34_out, not_35_out,
       not_36_out, not_37_out, not_38_out, not_39_out, not_40_out, not_41_out, not_42_out, not_43_out,
       not_44_out, not_45_out, not_46_out, not_47_out, not_48_out, not_49_out, or_1_out, or_2_out, or_3_out,
       or_4_out, or_5_out, or_6_out, or_7_out, or_8_out, or_9_out, or_10_out, or_11_out, or_12_out,
       or_13_out, or_14_out, or_15_out, or_16_out, or_17_out, or_18_out, or_19_out, or_20_out, or_21_out,
       or_22_out, or_23_out, or_24_out, or_25_out, or_26_out, or_27_out, or_28_out, s_r_ff_5_q, s_r_ff_6_q,
       s_r_ff_7_q, s_r_ff_8_q, s_r_ff_9_q, s_r_ff_10_q, s_r_ff_11_q, s_r_ff_12_q, s_r_ff_13_q, s_r_ff_14_q,
       s_r_ff_15_q, s_r_ff_16_q, s_r_ff_17_q, s_r_ff_18_q, s_r_ff_19_q, s_r_ff_20_q, s_r_ff_21_q,
       s_r_ff_22_q, s_r_ff_23_q, s_r_ff_24_q, s_r_ff_25_q, s_r_ff_26_q, s_r_ff_27_q, s_r_ff_28_q,
       s_r_ff_29_q, s_r_ff_30_q, s_r_ff_31_q, s_r_ff_32_q, s_r_ff_33_q, s_r_ff_34_q, s_r_ff_35_q, s_r_ff_36_q;

  and and_1 (and_1_out, MODE, CLK);
  D_Flip_Flop d_ff_1 (.D(MODE), .clk(CLK), .Q(d_ff_1_q));  // open: Qn, preset, reset
  S_R_Flip_Flop s_r_ff_1 (.S(or_25_out), .R(not_1_out), .clk(and_1_out), .Q(DOUT1));  // open: reset, Qn, preset
  not not_1 (not_1_out, or_25_out);
  S_R_Flip_Flop s_r_ff_2 (.S(or_26_out), .R(not_2_out), .clk(and_1_out), .Q(DOUT2));  // open: reset, Qn, preset
  not not_2 (not_2_out, or_26_out);
  S_R_Flip_Flop s_r_ff_3 (.S(or_27_out), .R(not_3_out), .clk(and_1_out), .Q(DOUT3));  // open: reset, Qn, preset
  not not_3 (not_3_out, or_27_out);
  S_R_Flip_Flop s_r_ff_4 (.S(or_28_out), .R(not_4_out), .clk(and_1_out), .Q(DOUT4));  // open: reset, Qn, preset
  not not_4 (not_4_out, or_28_out);
  D_Flip_Flop d_ff_2 (.D(ADDR1), .clk(CLK), .Q(d_ff_2_q));  // open: Qn, preset, reset
  D_Flip_Flop d_ff_3 (.D(ADDR2), .clk(CLK), .Q(d_ff_3_q));  // open: Qn, preset, reset
  D_Flip_Flop d_ff_4 (.D(ADDR3), .clk(CLK), .Q(d_ff_4_q));  // open: Qn, preset, reset
  not not_5 (not_5_out, d_ff_1_q);
  not not_6 (not_6_out, d_ff_4_q);
  not not_7 (not_7_out, d_ff_3_q);
  not not_8 (not_8_out, d_ff_2_q);
  not not_9 (not_9_out, d_ff_3_q);
  not not_10 (not_10_out, d_ff_2_q);
  not not_11 (not_11_out, d_ff_4_q);
  not not_12 (not_12_out, d_ff_2_q);
  not not_13 (not_13_out, d_ff_2_q);
  not not_14 (not_14_out, d_ff_4_q);
  not not_15 (not_15_out, d_ff_3_q);
  not not_16 (not_16_out, d_ff_3_q);
  not not_17 (not_17_out, d_ff_4_q);
  and and_2 (and_2_out, not_6_out, not_7_out, not_8_out);
  and and_3 (and_3_out, d_ff_4_q, not_9_out, not_10_out);
  and and_4 (and_4_out, not_11_out, d_ff_3_q, not_12_out);
  and and_5 (and_5_out, d_ff_4_q, d_ff_3_q, not_13_out);
  and and_6 (and_6_out, not_14_out, not_15_out, d_ff_2_q);
  and and_7 (and_7_out, d_ff_4_q, not_16_out, d_ff_2_q);
  and and_8 (and_8_out, not_17_out, d_ff_3_q, d_ff_2_q);
  and and_9 (and_9_out, d_ff_4_q, d_ff_3_q, d_ff_2_q);
  D_Flip_Flop d_ff_5 (.D(DIN1), .clk(CLK), .Q(d_ff_5_q));  // open: Qn, preset, reset
  D_Flip_Flop d_ff_6 (.D(DIN2), .clk(CLK), .Q(d_ff_6_q));  // open: Qn, preset, reset
  D_Flip_Flop d_ff_7 (.D(DIN3), .clk(CLK), .Q(d_ff_7_q));  // open: Qn, preset, reset
  D_Flip_Flop d_ff_8 (.D(DIN4), .clk(CLK), .Q(d_ff_8_q));  // open: Qn, preset, reset
  not not_18 (not_18_out, d_ff_5_q);
  not not_19 (not_19_out, d_ff_6_q);
  not not_20 (not_20_out, d_ff_7_q);
  not not_21 (not_21_out, d_ff_8_q);
  and and_10 (and_10_out, d_ff_5_q, and_2_out, not_5_out);
  and and_11 (and_11_out, not_18_out, and_2_out, not_5_out);
  and and_12 (and_12_out, d_ff_6_q, and_2_out, not_5_out);
  and and_13 (and_13_out, not_19_out, and_2_out, not_5_out);
  and and_14 (and_14_out, d_ff_7_q, and_2_out, not_5_out);
  and and_15 (and_15_out, not_20_out, and_2_out, not_5_out);
  and and_16 (and_16_out, d_ff_8_q, and_2_out, not_5_out);
  and and_17 (and_17_out, not_21_out, and_2_out, not_5_out);
  S_R_Flip_Flop s_r_ff_5 (.S(and_10_out), .R(and_11_out), .clk(CLK), .Q(s_r_ff_5_q));  // open: reset, Qn, preset
  S_R_Flip_Flop s_r_ff_6 (.S(and_12_out), .R(and_13_out), .clk(CLK), .Q(s_r_ff_6_q));  // open: reset, Qn, preset
  S_R_Flip_Flop s_r_ff_7 (.S(and_14_out), .R(and_15_out), .clk(CLK), .Q(s_r_ff_7_q));  // open: reset, Qn, preset
  S_R_Flip_Flop s_r_ff_8 (.S(and_16_out), .R(and_17_out), .clk(CLK), .Q(s_r_ff_8_q));  // open: reset, Qn, preset
  and and_18 (and_18_out, s_r_ff_5_q, and_2_out, d_ff_1_q, 1'b1);
  and and_19 (and_19_out, s_r_ff_6_q, and_2_out, d_ff_1_q, 1'b1);
  and and_20 (and_20_out, s_r_ff_7_q, and_2_out, d_ff_1_q, 1'b1);
  and and_21 (and_21_out, s_r_ff_8_q, and_2_out, d_ff_1_q, 1'b1);
  not not_22 (not_22_out, d_ff_5_q);
  not not_23 (not_23_out, d_ff_6_q);
  not not_24 (not_24_out, d_ff_7_q);
  not not_25 (not_25_out, d_ff_8_q);
  and and_22 (and_22_out, d_ff_5_q, and_3_out, not_5_out);
  and and_23 (and_23_out, not_22_out, and_3_out, not_5_out);
  and and_24 (and_24_out, d_ff_6_q, and_3_out, not_5_out);
  and and_25 (and_25_out, not_23_out, and_3_out, not_5_out);
  and and_26 (and_26_out, d_ff_7_q, and_3_out, not_5_out);
  and and_27 (and_27_out, not_24_out, and_3_out, not_5_out);
  and and_28 (and_28_out, d_ff_8_q, and_3_out, not_5_out);
  and and_29 (and_29_out, not_25_out, and_3_out, not_5_out);
  S_R_Flip_Flop s_r_ff_9 (.S(and_22_out), .R(and_23_out), .clk(CLK), .Q(s_r_ff_9_q));  // open: reset, Qn, preset
  S_R_Flip_Flop s_r_ff_10 (.S(and_24_out), .R(and_25_out), .clk(CLK), .Q(s_r_ff_10_q));  // open: reset, Qn, preset
  S_R_Flip_Flop s_r_ff_11 (.S(and_26_out), .R(and_27_out), .clk(CLK), .Q(s_r_ff_11_q));  // open: reset, Qn, preset
  S_R_Flip_Flop s_r_ff_12 (.S(and_28_out), .R(and_29_out), .clk(CLK), .Q(s_r_ff_12_q));  // open: reset, Qn, preset
  and and_30 (and_30_out, s_r_ff_9_q, and_3_out, d_ff_1_q, 1'b1);
  and and_31 (and_31_out, s_r_ff_10_q, and_3_out, d_ff_1_q, 1'b1);
  and and_32 (and_32_out, s_r_ff_11_q, and_3_out, d_ff_1_q, 1'b1);
  and and_33 (and_33_out, s_r_ff_12_q, and_3_out, d_ff_1_q, 1'b1);
  not not_26 (not_26_out, d_ff_5_q);
  not not_27 (not_27_out, d_ff_6_q);
  not not_28 (not_28_out, d_ff_7_q);
  not not_29 (not_29_out, d_ff_8_q);
  or or_1 (or_1_out, and_18_out, and_30_out);
  or or_2 (or_2_out, and_19_out, and_31_out);
  or or_3 (or_3_out, and_20_out, and_32_out);
  or or_4 (or_4_out, and_21_out, and_33_out);
  and and_34 (and_34_out, d_ff_5_q, and_4_out, not_5_out);
  and and_35 (and_35_out, not_26_out, and_4_out, not_5_out);
  and and_36 (and_36_out, d_ff_6_q, and_4_out, not_5_out);
  and and_37 (and_37_out, not_27_out, and_4_out, not_5_out);
  and and_38 (and_38_out, d_ff_7_q, and_4_out, not_5_out);
  and and_39 (and_39_out, not_28_out, and_4_out, not_5_out);
  and and_40 (and_40_out, d_ff_8_q, and_4_out, not_5_out);
  and and_41 (and_41_out, not_29_out, and_4_out, not_5_out);
  S_R_Flip_Flop s_r_ff_13 (.S(and_34_out), .R(and_35_out), .clk(CLK), .Q(s_r_ff_13_q));  // open: reset, Qn, preset
  S_R_Flip_Flop s_r_ff_14 (.S(and_36_out), .R(and_37_out), .clk(CLK), .Q(s_r_ff_14_q));  // open: reset, Qn, preset
  S_R_Flip_Flop s_r_ff_15 (.S(and_38_out), .R(and_39_out), .clk(CLK), .Q(s_r_ff_15_q));  // open: reset, Qn, preset
  S_R_Flip_Flop s_r_ff_16 (.S(and_40_out), .R(and_41_out), .clk(CLK), .Q(s_r_ff_16_q));  // open: reset, Qn, preset
  and and_42 (and_42_out, s_r_ff_13_q, and_4_out, d_ff_1_q, 1'b1);
  and and_43 (and_43_out, s_r_ff_14_q, and_4_out, d_ff_1_q, 1'b1);
  and and_44 (and_44_out, s_r_ff_15_q, and_4_out, d_ff_1_q, 1'b1);
  and and_45 (and_45_out, s_r_ff_16_q, and_4_out, d_ff_1_q, 1'b1);
  not not_30 (not_30_out, d_ff_5_q);
  not not_31 (not_31_out, d_ff_6_q);
  not not_32 (not_32_out, d_ff_7_q);
  not not_33 (not_33_out, d_ff_8_q);
  or or_5 (or_5_out, or_1_out, and_42_out);
  or or_6 (or_6_out, or_2_out, and_43_out);
  or or_7 (or_7_out, or_3_out, and_44_out);
  or or_8 (or_8_out, or_4_out, and_45_out);
  and and_46 (and_46_out, d_ff_5_q, and_5_out, not_5_out);
  and and_47 (and_47_out, not_30_out, and_5_out, not_5_out);
  and and_48 (and_48_out, d_ff_6_q, and_5_out, not_5_out);
  and and_49 (and_49_out, not_31_out, and_5_out, not_5_out);
  and and_50 (and_50_out, d_ff_7_q, and_5_out, not_5_out);
  and and_51 (and_51_out, not_32_out, and_5_out, not_5_out);
  and and_52 (and_52_out, d_ff_8_q, and_5_out, not_5_out);
  and and_53 (and_53_out, not_33_out, and_5_out, not_5_out);
  S_R_Flip_Flop s_r_ff_17 (.S(and_46_out), .R(and_47_out), .clk(CLK), .Q(s_r_ff_17_q));  // open: reset, Qn, preset
  S_R_Flip_Flop s_r_ff_18 (.S(and_48_out), .R(and_49_out), .clk(CLK), .Q(s_r_ff_18_q));  // open: reset, Qn, preset
  S_R_Flip_Flop s_r_ff_19 (.S(and_50_out), .R(and_51_out), .clk(CLK), .Q(s_r_ff_19_q));  // open: reset, Qn, preset
  S_R_Flip_Flop s_r_ff_20 (.S(and_52_out), .R(and_53_out), .clk(CLK), .Q(s_r_ff_20_q));  // open: reset, Qn, preset
  and and_54 (and_54_out, s_r_ff_17_q, and_5_out, d_ff_1_q, 1'b1);
  and and_55 (and_55_out, s_r_ff_18_q, and_5_out, d_ff_1_q, 1'b1);
  and and_56 (and_56_out, s_r_ff_19_q, and_5_out, d_ff_1_q, 1'b1);
  and and_57 (and_57_out, s_r_ff_20_q, and_5_out, d_ff_1_q, 1'b1);
  not not_34 (not_34_out, d_ff_5_q);
  not not_35 (not_35_out, d_ff_6_q);
  not not_36 (not_36_out, d_ff_7_q);
  not not_37 (not_37_out, d_ff_8_q);
  or or_9 (or_9_out, or_5_out, and_54_out);
  or or_10 (or_10_out, or_6_out, and_55_out);
  or or_11 (or_11_out, or_7_out, and_56_out);
  or or_12 (or_12_out, or_8_out, and_57_out);
  S_R_Flip_Flop s_r_ff_21 (.S(and_58_out), .R(and_59_out), .clk(CLK), .Q(s_r_ff_21_q));  // open: reset, Qn, preset
  and and_58 (and_58_out, d_ff_5_q, and_6_out, not_5_out);
  and and_59 (and_59_out, not_34_out, and_6_out, not_5_out);
  S_R_Flip_Flop s_r_ff_22 (.S(and_60_out), .R(and_61_out), .clk(CLK), .Q(s_r_ff_22_q));  // open: reset, Qn, preset
  and and_60 (and_60_out, d_ff_6_q, and_6_out, not_5_out);
  and and_61 (and_61_out, not_35_out, and_6_out, not_5_out);
  S_R_Flip_Flop s_r_ff_23 (.S(and_62_out), .R(and_63_out), .clk(CLK), .Q(s_r_ff_23_q));  // open: reset, Qn, preset
  and and_62 (and_62_out, d_ff_7_q, and_6_out, not_5_out);
  and and_63 (and_63_out, not_36_out, and_6_out, not_5_out);
  S_R_Flip_Flop s_r_ff_24 (.S(and_64_out), .R(and_65_out), .clk(CLK), .Q(s_r_ff_24_q));  // open: reset, Qn, preset
  and and_64 (and_64_out, d_ff_8_q, and_6_out, not_5_out);
  and and_65 (and_65_out, not_37_out, and_6_out, not_5_out);
  and and_66 (and_66_out, s_r_ff_21_q, and_6_out, d_ff_1_q, 1'b1);
  and and_67 (and_67_out, s_r_ff_22_q, and_6_out, d_ff_1_q, 1'b1);
  and and_68 (and_68_out, s_r_ff_23_q, and_6_out, d_ff_1_q, 1'b1);
  and and_69 (and_69_out, s_r_ff_24_q, and_6_out, d_ff_1_q, 1'b1);
  not not_38 (not_38_out, d_ff_5_q);
  not not_39 (not_39_out, d_ff_6_q);
  not not_40 (not_40_out, d_ff_7_q);
  not not_41 (not_41_out, d_ff_8_q);
  or or_13 (or_13_out, or_9_out, and_66_out);
  or or_14 (or_14_out, or_10_out, and_67_out);
  or or_15 (or_15_out, or_11_out, and_68_out);
  or or_16 (or_16_out, or_12_out, and_69_out);
  and and_70 (and_70_out, d_ff_5_q, and_7_out, not_5_out);
  and and_71 (and_71_out, not_38_out, and_7_out, not_5_out);
  and and_72 (and_72_out, d_ff_6_q, and_7_out, not_5_out);
  and and_73 (and_73_out, not_39_out, and_7_out, not_5_out);
  and and_74 (and_74_out, d_ff_7_q, and_7_out, not_5_out);
  and and_75 (and_75_out, not_40_out, and_7_out, not_5_out);
  and and_76 (and_76_out, d_ff_8_q, and_7_out, not_5_out);
  and and_77 (and_77_out, not_41_out, and_7_out, not_5_out);
  S_R_Flip_Flop s_r_ff_25 (.S(and_70_out), .R(and_71_out), .clk(CLK), .Q(s_r_ff_25_q));  // open: reset, Qn, preset
  S_R_Flip_Flop s_r_ff_26 (.S(and_72_out), .R(and_73_out), .clk(CLK), .Q(s_r_ff_26_q));  // open: reset, Qn, preset
  S_R_Flip_Flop s_r_ff_27 (.S(and_74_out), .R(and_75_out), .clk(CLK), .Q(s_r_ff_27_q));  // open: reset, Qn, preset
  S_R_Flip_Flop s_r_ff_28 (.S(and_76_out), .R(and_77_out), .clk(CLK), .Q(s_r_ff_28_q));  // open: reset, Qn, preset
  and and_78 (and_78_out, s_r_ff_25_q, and_7_out, d_ff_1_q, 1'b1);
  and and_79 (and_79_out, s_r_ff_26_q, and_7_out, d_ff_1_q, 1'b1);
  and and_80 (and_80_out, s_r_ff_27_q, and_7_out, d_ff_1_q, 1'b1);
  and and_81 (and_81_out, s_r_ff_28_q, and_7_out, d_ff_1_q, 1'b1);
  not not_42 (not_42_out, d_ff_5_q);
  not not_43 (not_43_out, d_ff_6_q);
  not not_44 (not_44_out, d_ff_7_q);
  not not_45 (not_45_out, d_ff_8_q);
  or or_17 (or_17_out, or_13_out, and_78_out);
  or or_18 (or_18_out, or_14_out, and_79_out);
  or or_19 (or_19_out, or_15_out, and_80_out);
  or or_20 (or_20_out, or_16_out, and_81_out);
  and and_82 (and_82_out, d_ff_5_q, and_8_out, not_5_out);
  and and_83 (and_83_out, not_42_out, and_8_out, not_5_out);
  and and_84 (and_84_out, d_ff_6_q, and_8_out, not_5_out);
  and and_85 (and_85_out, not_43_out, and_8_out, not_5_out);
  and and_86 (and_86_out, d_ff_7_q, and_8_out, not_5_out);
  and and_87 (and_87_out, not_44_out, and_8_out, not_5_out);
  and and_88 (and_88_out, d_ff_8_q, and_8_out, not_5_out);
  and and_89 (and_89_out, not_45_out, and_8_out, not_5_out);
  S_R_Flip_Flop s_r_ff_29 (.S(and_82_out), .R(and_83_out), .clk(CLK), .Q(s_r_ff_29_q));  // open: reset, Qn, preset
  S_R_Flip_Flop s_r_ff_30 (.S(and_84_out), .R(and_85_out), .clk(CLK), .Q(s_r_ff_30_q));  // open: reset, Qn, preset
  S_R_Flip_Flop s_r_ff_31 (.S(and_86_out), .R(and_87_out), .clk(CLK), .Q(s_r_ff_31_q));  // open: reset, Qn, preset
  S_R_Flip_Flop s_r_ff_32 (.S(and_88_out), .R(and_89_out), .clk(CLK), .Q(s_r_ff_32_q));  // open: reset, Qn, preset
  and and_90 (and_90_out, s_r_ff_29_q, and_8_out, d_ff_1_q, 1'b1);
  and and_91 (and_91_out, s_r_ff_30_q, and_8_out, d_ff_1_q, 1'b1);
  and and_92 (and_92_out, s_r_ff_31_q, and_8_out, d_ff_1_q, 1'b1);
  and and_93 (and_93_out, s_r_ff_32_q, and_8_out, d_ff_1_q, 1'b1);
  not not_46 (not_46_out, d_ff_5_q);
  not not_47 (not_47_out, d_ff_6_q);
  not not_48 (not_48_out, d_ff_7_q);
  not not_49 (not_49_out, d_ff_8_q);
  or or_21 (or_21_out, or_17_out, and_90_out);
  or or_22 (or_22_out, or_18_out, and_91_out);
  or or_23 (or_23_out, or_19_out, and_92_out);
  or or_24 (or_24_out, or_20_out, and_93_out);
  and and_94 (and_94_out, d_ff_5_q, and_9_out, not_5_out);
  and and_95 (and_95_out, not_46_out, and_9_out, not_5_out);
  and and_96 (and_96_out, d_ff_6_q, and_9_out, not_5_out);
  and and_97 (and_97_out, not_47_out, and_9_out, not_5_out);
  and and_98 (and_98_out, d_ff_7_q, and_9_out, not_5_out);
  and and_99 (and_99_out, not_48_out, and_9_out, not_5_out);
  and and_100 (and_100_out, d_ff_8_q, and_9_out, not_5_out);
  and and_101 (and_101_out, not_49_out, and_9_out, not_5_out);
  S_R_Flip_Flop s_r_ff_33 (.S(and_94_out), .R(and_95_out), .clk(CLK), .Q(s_r_ff_33_q));  // open: reset, Qn, preset
  S_R_Flip_Flop s_r_ff_34 (.S(and_96_out), .R(and_97_out), .clk(CLK), .Q(s_r_ff_34_q));  // open: reset, Qn, preset
  S_R_Flip_Flop s_r_ff_35 (.S(and_98_out), .R(and_99_out), .clk(CLK), .Q(s_r_ff_35_q));  // open: reset, Qn, preset
  S_R_Flip_Flop s_r_ff_36 (.S(and_100_out), .R(and_101_out), .clk(CLK), .Q(s_r_ff_36_q));  // open: reset, Qn, preset
  and and_102 (and_102_out, s_r_ff_33_q, and_9_out, d_ff_1_q, 1'b1);
  and and_103 (and_103_out, s_r_ff_34_q, and_9_out, d_ff_1_q, 1'b1);
  and and_104 (and_104_out, s_r_ff_35_q, and_9_out, d_ff_1_q, 1'b1);
  and and_105 (and_105_out, s_r_ff_36_q, and_9_out, d_ff_1_q, 1'b1);
  or or_25 (or_25_out, or_21_out, and_102_out);
  or or_26 (or_26_out, or_22_out, and_103_out);
  or or_27 (or_27_out, or_23_out, and_104_out);
  or or_28 (or_28_out, or_24_out, and_105_out);

  // Notes on the sheet:
  //   Mode
  //   This should be 1 for the circuit to work
  //   Address
  //   John Hsu
  //   261169005
  //   This was connected to the clock before, but that implementation didn't work
  //   Removing this wire means I have to change all the AND gates so instead I used a constant here
  //   Data In
  //   Data Out
endmodule

module cu (
  input  in_1,
  input  in_2,
  input  Inputbit2,
  input  Inputbit1,
  output LRin,
  output ALUOP,
  output WriteMem,
  output WriteReg,
  output Memtoreg,
  output MemRead
);

  wire add_out, and_1_out, and_2_out, and_4_out, and_5_out, and_6_out, and_9_out, and_10_out, and_11_out,
       and_13_out, and_14_out, and_15_out, Load_out, not_1_out, not_2_out, not_3_out, not_4_out, not_5_out,
       not_6_out, not_7_out, not_8_out, not_9_out, not_10_out, not_11_out, not_12_out, not_13_out,
       not_14_out, not_15_out, not_16_out, not_17_out, not_18_out, not_19_out, not_20_out, save_out, sub_out;

  Clock clock_1 ();  // open: out
  not not_1 (not_1_out, Inputbit1);
  not not_2 (not_2_out, Inputbit2);
  not not_3 (not_3_out, Inputbit2);
  not not_4 (not_4_out, Inputbit1);
  and add (add_out, not_4_out, Inputbit2);
  and sub (sub_out, Inputbit1, Inputbit2);
  and save (save_out, Inputbit1, not_3_out);
  and Load (Load_out, not_1_out, not_2_out);
  not not_5 (not_5_out, in_2);
  not not_6 (not_6_out, in_1);
  not not_7 (not_7_out, in_1);
  not not_8 (not_8_out, in_2);
  not not_9 (not_9_out, in_2);
  not not_10 (not_10_out, in_1);
  not not_11 (not_11_out, in_1);
  not not_12 (not_12_out, in_2);
  not not_13 (not_13_out, in_2);
  not not_14 (not_14_out, in_1);
  not not_15 (not_15_out, in_1);
  not not_16 (not_16_out, in_2);
  not not_17 (not_17_out, in_2);
  not not_18 (not_18_out, in_1);
  not not_19 (not_19_out, in_1);
  not not_20 (not_20_out, in_2);
  and and_1 (and_1_out, Load_out, not_5_out, not_6_out);
  and and_2 (and_2_out, Load_out, in_2, not_7_out);
  and and_3 (MemRead, Load_out, not_8_out, in_1);
  and and_4 (and_4_out, Load_out, in_2, in_1);
  and and_5 (and_5_out, save_out, not_9_out, not_10_out);
  and and_6 (and_6_out, save_out, in_2, not_11_out);
  and and_7 (WriteMem, save_out, not_12_out, in_1);
  // AND_Gate and_8 has open pins: in0=save_out, in1=in_2, in2=in_1, out=open
  and and_9 (and_9_out, add_out, not_13_out, not_14_out);
  and and_10 (and_10_out, add_out, in_2, not_15_out);
  and and_11 (and_11_out, add_out, not_16_out, in_1);
  // AND_Gate and_12 has open pins: in0=add_out, in1=in_2, in2=in_1, out=open
  and and_13 (and_13_out, sub_out, not_17_out, not_18_out);
  and and_14 (and_14_out, sub_out, in_2, not_19_out);
  and and_15 (and_15_out, sub_out, not_20_out, in_1);
  // AND_Gate and_16 has open pins: in0=sub_out, in1=in_2, in2=in_1, out=open
  or or_1 (LRin, and_1_out, and_13_out, and_9_out, and_5_out);
  or or_2 (ALUOP, and_2_out, and_6_out, and_10_out, and_14_out);
  or or_3 (WriteReg, and_15_out, and_4_out, and_11_out);
  Clock clock_2 ();  // open: out
  Clock clock_3 ();  // open: out

  assign Memtoreg = MemRead;
endmodule
